# Fritzing sketch Conexion (saved by Fritzing 0.9.3b)

parts:
  Componente1 = Alhambra II - V 1.0A
  U1 = ESP8266 ESP-01 Upgraded WiFi Module [part_number=ESP8266]

nets:
  N1: Componente1.D0, Componente1.S0, Componente1.3V3, U1.CH_PD, U1.TXD
  N2: Componente1.D1, Componente1.S1, U1.RXD
  N3: Componente1.G0, U1.GND

notes:
  Atención el modulo funciona a 3.3v
  RX
  GND
  TX

custom parts:
  Alhambra II - V 1.0A: Open FPGA electronic board. Synthesize hardware easily, using only open source tools
  ESP8266 ESP-01 Upgraded WiFi Module: Upgraded Version ESP-01,all Flash are upgraded to 1M byte.Also support Cloud service remote transmission.
